# Fritzing sketch ardsig (saved by Fritzing 0.9.3b)
circuit board: 8.46667cm x 5.64444cm
breadboards: 1

parts:
  Часть1 = Arduino Nano (Rev3.0)
  Часть2 = Adafruit DS3231 [part_number="Adafruit #3013"]
  Часть3 = HC-SR501 Body Sensor Module
  DHT1 = DHT11 Humitidy and Temperature Sensor
  Reg1 = DC-DC CONVERTER [part_number=80633 package=dc-dc_converter]
  SIM800L_BO1 = SIM800L BO
  Power_plug1 = Power plug
  Reg2 = DC-DC CONVERTER [part_number=80633 package=dc-dc_converter]
  KY-1 = Keyes Relay [package=THT]
  S1 = SWITCH-MOMENTARY-2 [package=reed_switch_plastic]
  R1 = Resistor [tolerance=±5% resistance=220 package=THT]
  J1 = Piezo Speaker  # not connected

nets (from the breadboard view):
  GND: Часть1.GND, DHT1.GND, Reg1.IN-, Power_plug1.GND, Reg2.IN-, R1.Pin_0
  N1: Часть1.D2, S1.1, R1.Pin_1
  N2: Часть1.D3, DHT1.DATA
  N3: Часть1.D6, Часть3.OUT
  N4: Часть1.D7, KY-1.signal
  N5: Часть1.D8, SIM800L_BO1.pin_5
  N6: Часть1.D9, SIM800L_BO1.pin_4
  VIN: Часть1.VIN, Reg1.IN+, Power_plug1.VCC, Reg2.IN+
  5V: Часть1.5V, Часть3.VCC, DHT1.VDD
  N7: Часть1.A5, Часть2.SCL
  N8: Часть1.A4, Часть2.SDA
  N9: Часть2.Vin, Reg1.OUT+, KY-1.power
  GND_2: Часть2.GND, Часть3.GND, Reg1.OUT-, KY-1.ground
  N10: SIM800L_BO1.PIN2, Reg2.OUT+
  N11: SIM800L_BO1.pin_6, Reg2.OUT-

custom parts:
  Adafruit DS3231: The datasheet for the DS3231 explains that this part is an "Extremely Accurate I²C-Integrated RTC/TCXO/Crystal". And, hey, it does exactly what it says on the tin! This Real Time Clock (RTC) is the most precise you can get in a small, low power package. Most RTCs use an external 32kHz timing crystal that is used to keep time with low current draw. And that's all well and good, but those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
  HC-SR501 Body Sensor Module: Pyroelectric Infrared PIR Motion Sensor Detector Module
  DHT11 Humitidy and Temperature Sensor: DHT11 Humidity and Temperature Sensor
  DC-DC CONVERTER: WYHP 5A constant current/voltage manufactured by Shenzhen Weiyapuhua Technology Co., Ltd
  Keyes Relay: The Keyes 5V relay module is suitable for SCM development, home appliance control. It uses a 5V~12V TIL control signal which can control DC / AC signal.
